# Fritzing sketch robot_sketch (saved by Fritzing 0.9.3b)
breadboards: 2

parts:
  U1 = LuaNode32 / ESP32
  BAT1 = BC9VPC [package=bc9vpc]
  U2 = Mini-360 DC-DC Buck converter [package=THT]
  U3 = SWITCH_SPDT [package=kps-1290]
  LED1 = LEDs [package=led10mm]
  LED2 = LEDs [package=led10mm]
  R1 = Resistor [tolerance=±5% resistance=220 package="0603 [SMD]"]
  R2 = Resistor [tolerance=±5% resistance=220 package="0603 [SMD]"]
  U4 = CAPSENSE_PAD [package=capsense_pad]
  U5 = CAPSENSE_PAD [package=capsense_pad]
  U6 = CAPSENSE_PAD [package=capsense_pad]
  U7 = CAPSENSE_PAD [package=capsense_pad]
  Part1 = HC-SR501 Body Sensor Module
  JQ1 = JQ6500
  SP1 = SPEAKER [package=pcb_mount_speaker]  # not connected

nets:
  N1: U1.D33, U5.RECEIVE
  N2: U1.D12, U4.RECEIVE
  N3: U1.D13, U6.RECEIVE
  GND: U1.GND, U2.OUT-, LED1.A, LED2.C, Part1.GND, JQ1.GND
  VIN: U1.Vin, U3.S, Part1.VCC
  N4: U1.D15, U7.RECEIVE
  N5: U1.D21, Part1.OUT
  N6: U1.D22, R2.Pin_0
  N7: U1.D23, R1.Pin_0
  N8: BAT1.V+, U2.IN+
  N9: BAT1.V-, U2.IN-
  N10: U2.OUT+, U3.P
  N11: LED1.C, R1.Pin_1
  N12: LED2.A, R2.Pin_1

custom parts:
  LuaNode32 / ESP32: ESP32 based LuaNode32
  Mini-360 DC-DC Buck converter: Mini-360 DC-DC Buck converter. Tiny buck step down voltage converter, input voltage 4.75 to 23V output 1 to 17V adjustable. Available from ebay and the like.
  HC-SR501 Body Sensor Module: Pyroelectric Infrared PIR Motion Sensor Detector Module
